// Logisim project memoria.circ as structural Verilog: 1 circuit, main circuit main
module main (
  input  Teste_igualdade,
  input  clear,
  output out_3,
  output [15:0] out_4,
  output Indica_se_terminou_a_contagem,
  output [7:0] out_6,
  output [7:0] out_7
);

  wire \_1_armazena__0_lê_out , clock_1_out, comparator_1_eq, not_1_out;
  wire [15:0] counter_1_q;

  Counter #(.width(16), .ongoal("load")) counter_1 (
    .load(Teste_igualdade), .D(16'hffaf), .Q(counter_1_q), .carry(Indica_se_terminou_a_contagem),
    .clk(clock_1_out), .clr(clear));  // open: count
  Clock clock_1 (.out(clock_1_out));
  Register #(.width(1)) register_1 (.D(1'b1), .Q(out_3), .clk(Indica_se_terminou_a_contagem), .clr(clear));  // open: en
  Register register_2 (.D(counter_1_q[15:8]), .Q(out_4[15:8]), .clk(clock_1_out), .clr(clear));  // open: en
  Register menos_sig (.D(counter_1_q[7:0]), .Q(out_4[7:0]), .clk(clock_1_out), .clr(clear));  // open: en
  not not_1 (not_1_out, comparator_1_eq);
  Comparator #(.mode("unsigned")) comparator_1 (.a(out_4[7:0]), .b(out_6), .eq(comparator_1_eq));  // open: gt, lt
  not \_1_armazena__0_lê  (\_1_armazena__0_lê_out , out_3);
  LED \Entrada_e_saída_iguais  (.in(not_1_out));
  RAM #(.addrWidth(16), .bus("separate")) ram_1 (
    .addr(out_4), .din(out_4[7:0]), .data(out_6), .str(\_1_armazena__0_lê_out ), .clk(clock_1_out),
    .clr(clear));  // open: sel, ld

  assign out_7 = out_4[7:0];

  // Notes on the sheet:
  //   endereçamento
  //   entrada de dados
endmodule
